// Logisim project aois33.circ as structural Verilog: 1 circuit, main circuit main
module main (
  input  V,
  output Q1,
  output Q2,
  output Q3
);

  wire and_1_out, and_2_out, clock_1_out;

  Clock clock_1 (.out(clock_1_out));
  T_Flip_Flop T1 (.T(V), .clk(clock_1_out), .Q(Q1));  // open: Qn, reset, preset
  and and_1 (and_1_out, Q1, V);
  T_Flip_Flop T2 (.T(and_1_out), .clk(clock_1_out), .Q(Q2));  // open: Qn, reset, preset
  and and_2 (and_2_out, V, Q1, Q2);
  T_Flip_Flop T3 (.T(and_2_out), .clk(clock_1_out), .Q(Q3));  // open: Qn, reset, preset
endmodule
