// Logisim project aois3_1.circ as structural Verilog: 2 circuits, main circuit ods1bit
module ods1bit (
  input  A,
  input  B,
  input  Cin,
  output S,
  output Cout
);

  wire not_1_out, not_2_out, not_3_out, or_1_out, or_2_out, or_3_out, or_4_out, or_5_out, or_6_out, or_7_out;

  not not_1 (not_1_out, A);
  not not_2 (not_2_out, B);
  not not_3 (not_3_out, Cin);
  or or_1 (or_1_out, A, B, Cin);
  or or_2 (or_2_out, A, not_2_out, not_3_out);
  or or_3 (or_3_out, not_1_out, B, not_3_out);
  or or_4 (or_4_out, not_1_out, not_2_out, Cin);
  or or_5 (or_5_out, A, B);
  or or_6 (or_6_out, A, Cin);
  or or_7 (or_7_out, B, Cin);
  and and_1 (S, or_1_out, or_2_out, or_3_out, or_4_out);
  and and_2 (Cout, or_5_out, or_6_out, or_7_out);
endmodule

module ODS8bit (
  input  [7:0] A,
  input  [7:0] B,
  output Overflow,
  output [7:0] S
);

  wire ods1bit_2_cout, ods1bit_3_cout, ods1bit_4_cout, ods1bit_5_cout, ods1bit_6_cout, ods1bit_7_cout,
       ods1bit_8_cout;

  ods1bit ods1bit_1 (.A(A[7]), .B(B[7]), .Cin(ods1bit_2_cout), .S(S[7]), .Cout(Overflow));
  ods1bit ods1bit_2 (.A(A[6]), .B(B[6]), .Cin(ods1bit_3_cout), .S(S[6]), .Cout(ods1bit_2_cout));
  ods1bit ods1bit_3 (.A(A[5]), .B(B[5]), .Cin(ods1bit_4_cout), .S(S[5]), .Cout(ods1bit_3_cout));
  ods1bit ods1bit_4 (.A(A[4]), .B(B[4]), .Cin(ods1bit_5_cout), .S(S[4]), .Cout(ods1bit_4_cout));
  ods1bit ods1bit_5 (.A(A[3]), .B(B[3]), .Cin(ods1bit_6_cout), .S(S[3]), .Cout(ods1bit_5_cout));
  ods1bit ods1bit_6 (.A(A[2]), .B(B[2]), .Cin(ods1bit_7_cout), .S(S[2]), .Cout(ods1bit_6_cout));
  ods1bit ods1bit_7 (.A(A[1]), .B(B[1]), .Cin(ods1bit_8_cout), .S(S[1]), .Cout(ods1bit_7_cout));
  ods1bit ods1bit_8 (.A(A[0]), .B(B[0]), .Cin(1'b0), .S(S[0]), .Cout(ods1bit_8_cout));
endmodule
