// Logisim project aois3_2.circ as structural Verilog: 3 circuits, main circuit main
module main (
  input  [3:0] in_1,
  input  [3:0] in_2,
  output [1:0] out_3,
  output [3:0] out_4
);

  wire adder_1_cout;
  wire [3:0] adder_1_out, decoder_2421_1_b0, decoder_2421_2_b0;

  Decoder_2421 decoder_2421_1 (
    .a3(in_1[3]), .a2(in_1[2]), .a1(in_1[1]), .a0(in_1[0]), .b3(decoder_2421_1_b0[3]),
    .b2(decoder_2421_1_b0[2]), .b1(decoder_2421_1_b0[1]), .b0(decoder_2421_1_b0[0]));
  Decoder_2421 decoder_2421_2 (
    .a3(in_2[3]), .a2(in_2[2]), .a1(in_2[1]), .a0(in_2[0]), .b3(decoder_2421_2_b0[3]),
    .b2(decoder_2421_2_b0[2]), .b1(decoder_2421_2_b0[1]), .b0(decoder_2421_2_b0[0]));
  Adder #(.width(4)) adder_1 (
    .a(decoder_2421_1_b0), .b(decoder_2421_2_b0), .out(adder_1_out), .cin(1'b1), .cout(adder_1_cout));
  Encoder_2421 encoder_2421_1 (
    .cin(adder_1_cout), .a3(adder_1_out[3]), .a2(adder_1_out[2]), .a1(adder_1_out[1]), .a0(adder_1_out[0]),
    .Pout2(out_3[0]), .Pout(out_3[1]), .b3(out_4[3]), .b2(out_4[2]), .b1(out_4[1]), .b0(out_4[0]));
endmodule

module Decoder_2421 (
  input  a3,
  input  a2,
  input  a1,
  input  a0,
  output b3,
  output b2,
  output b1,
  output b0
);

  wire and_2_out, and_3_out, and_4_out, and_5_out, and_6_out, not_1_out, not_2_out, not_3_out;

  not not_1 (not_1_out, a3);
  not not_2 (not_2_out, a2);
  not not_3 (not_3_out, a1);
  and and_1 (b3, a3, a2, a1);
  and and_2 (and_2_out, not_1_out, a2);
  and and_3 (and_3_out, a3, not_2_out, a1);
  and and_4 (and_4_out, a2, not_3_out);
  and and_5 (and_5_out, not_1_out, a1);
  and and_6 (and_6_out, a3, not_3_out);
  or or_1 (b2, and_2_out, and_3_out, and_4_out);
  or or_2 (b1, and_5_out, and_6_out);

  assign b0 = a0;
endmodule

module Encoder_2421 (
  input  cin,
  input  a3,
  input  a2,
  input  a1,
  input  a0,
  output Pout2,
  output Pout,
  output b3,
  output b2,
  output b1,
  output b0
);

  wire and_1_out, and_2_out, and_3_out, and_4_out, and_5_out, and_6_out, and_7_out, and_8_out, and_9_out,
       and_10_out, and_11_out, and_12_out, and_13_out, and_14_out, and_15_out, and_16_out, and_17_out,
       and_18_out, and_19_out, and_20_out, and_21_out, and_22_out, and_23_out, and_24_out, and_25_out,
       and_26_out, and_27_out, not_1_out, not_2_out, not_3_out, not_4_out, not_5_out;

  not not_1 (not_1_out, cin);
  not not_2 (not_2_out, a3);
  not not_3 (not_3_out, a2);
  not not_4 (not_4_out, a1);
  not not_5 (not_5_out, a0);
  and and_1 (and_1_out, a3, a1);
  and and_2 (and_2_out, a3, a2);
  and and_3 (and_3_out, not_2_out, a2, a0);
  and and_4 (and_4_out, not_2_out, a2, a1);
  and and_5 (and_5_out, a3, not_3_out, not_4_out);
  and and_6 (and_6_out, a2, a1, a0);
  and and_7 (and_7_out, cin, not_2_out, not_3_out);
  and and_8 (and_8_out, cin, a3, not_5_out);
  and and_9 (and_9_out, cin, a3, a2);
  and and_10 (and_10_out, not_1_out, not_2_out, a2, not_5_out);
  and and_11 (and_11_out, not_2_out, a2, a1);
  and and_12 (and_12_out, a3, not_3_out, not_4_out);
  and and_13 (and_13_out, a2, a1, not_5_out);
  and and_14 (and_14_out, cin, not_3_out);
  and and_15 (and_15_out, cin, a3);
  and and_16 (and_16_out, not_1_out, not_2_out, not_3_out, a1);
  and and_17 (and_17_out, not_2_out, not_3_out, a1, a0);
  and and_18 (and_18_out, not_2_out, a2, not_4_out, a0);
  and and_19 (and_19_out, a3, not_3_out, not_4_out);
  and and_20 (and_20_out, cin, a3, not_5_out);
  and and_21 (and_21_out, not_1_out, a3, not_4_out);
  and and_22 (and_22_out, a3, a2, a1, a0);
  and and_23 (and_23_out, not_1_out, a0);
  and and_24 (and_24_out, not_2_out, a0);
  and and_25 (and_25_out, not_3_out, not_4_out, a0);
  and and_26 (and_26_out, cin, a3, a1, not_5_out);
  and and_27 (and_27_out, cin, a3, a2, not_5_out);
  or or_1 (Pout, cin, and_1_out, and_2_out);
  or or_2 (b3, and_3_out, and_4_out, and_5_out, and_6_out, and_7_out, and_8_out, and_9_out);
  or or_3 (b2, and_10_out, and_11_out, and_12_out, and_13_out, and_14_out, and_15_out);
  or or_4 (b1, and_16_out, and_17_out, and_18_out, and_19_out, and_20_out, and_21_out, and_22_out);
  or or_5 (b0, and_23_out, and_24_out, and_25_out, and_26_out, and_27_out);

  assign Pout2 = 1'b0;
endmodule
